# Fritzing sketch LedComPotenciometro (saved by Fritzing 0.7.10b)
breadboards: 1

parts:
  LED1 = LED - 5mm [color="Red (633nm)" package="5 mm [THT]"]
  Arduino1 = Arduino
  R1 = Resistor [tolerance=±5% resistance=220 package=THT]
  R2 = Rotary Potentiometer (Small) [maximum_resistance=100kΩ]

nets:
  N1: LED1.cathode, Arduino1.GND, R2.leg2
  N2: LED1.anode, R1.Pin_0
  N3: Arduino1.D11, R1.Pin_1
  N4: Arduino1.+5V, R2.leg1
  N5: Arduino1.A0, R2.wiper
